# Fritzing sketch Blink_LED (saved by Fritzing 0.9.3b)
breadboards: 1

parts:
  LED1 = LED - 3mm [color="Red (633nm)" package="3 mm [THT]"]
  Raspberry_Pi_1 = Raspberry Pi 3 [part_number=RPI-3-V1.2]
  R1 = Resistor [tolerance=±5% resistance=1k package="2010 [SMD]"]

nets:
  N1: LED1.cathode, R1.Pin_0
  N2: LED1.anode, Raspberry_Pi_1.GPIO23
  N3: Raspberry_Pi_1.GND, R1.Pin_1
