# Fritzing sketch 2Way_Switch (saved by Fritzing 0.9.3b)
breadboards: 1

parts:
  Raspberry_Pi_1 = Raspberry Pi 3 [part_number=RPI-3-V1.2]
  S1 = Toggle Switch [package=THT]
  R1 = Resistor [tolerance=±5% resistance=10k package="2010 [SMD]"]
  R2 = Resistor [tolerance=±5% resistance=10k package="2010 [SMD]"]

nets:
  N1: Raspberry_Pi_1.GPIO17, S1.L1, R1.Pin_0
  N2: Raspberry_Pi_1.GPIO27, S1.L2, R2.Pin_0
  N3: Raspberry_Pi_1.3V3, S1.COM
  N4: Raspberry_Pi_1.GND, R1.Pin_1, R2.Pin_1
