# Fritzing sketch Light_Bar_Graph (saved by Fritzing 0.9.3b)
breadboards: 1

parts:
  Raspberry_Pi_1 = Raspberry Pi 3 [part_number=RPI-3-V1.2]
  D1 = LED_BARGRAPH_10 [package=led_bargaph_10]
  R3 = Resistor [tolerance=±5% resistance=1k package="2010 [SMD]"]
  R4 = Resistor [tolerance=±5% resistance=1k package="2010 [SMD]"]
  R5 = Resistor [tolerance=±5% resistance=1k package="2010 [SMD]"]
  R6 = Resistor [tolerance=±5% resistance=1k package="2010 [SMD]"]
  R7 = Resistor [tolerance=±5% resistance=1k package="2010 [SMD]"]
  R8 = Resistor [tolerance=±5% resistance=1k package="2010 [SMD]"]
  R9 = Resistor [tolerance=±5% resistance=1k package="2010 [SMD]"]
  R10 = Resistor [tolerance=±5% resistance=1k package="2010 [SMD]"]
  R11 = Resistor [tolerance=±5% resistance=1k package="2010 [SMD]"]
  R12 = Resistor [tolerance=±5% resistance=1k package="2010 [SMD]"]

nets:
  N1: Raspberry_Pi_1.GPIO12, D1.J_C
  N2: Raspberry_Pi_1.ID_SC, D1.I_C
  N3: Raspberry_Pi_1.GPIO7, D1.H_C
  N4: Raspberry_Pi_1.GPIO8, D1.G_C
  N5: Raspberry_Pi_1.GPIO25, D1.F_C
  N6: Raspberry_Pi_1.GPIO24, D1.E_C
  N7: Raspberry_Pi_1.GPIO23, D1.D_C
  N8: Raspberry_Pi_1.GPIO18, D1.C_C
  N9: Raspberry_Pi_1.GPIO15, D1.B_C
  N10: Raspberry_Pi_1.GPIO14, D1.A_C
  N11: Raspberry_Pi_1.GND, R3.Pin_1, R4.Pin_1, R5.Pin_1, R6.Pin_1, R7.Pin_0, R8.Pin_0, R9.Pin_0, R10.Pin_0, R11.Pin_0, R12.Pin_1
  N12: D1.A_A, R11.Pin_1
  N13: D1.B_A, R7.Pin_1
  N14: D1.C_A, R8.Pin_1
  N15: D1.D_A, R9.Pin_1
  N16: D1.E_A, R10.Pin_1
  N17: D1.F_A, R12.Pin_0
  N18: D1.G_A, R6.Pin_0
  N19: D1.H_A, R5.Pin_0
  N20: D1.I_A, R4.Pin_0
  N21: D1.J_A, R3.Pin_0
