# Fritzing sketch XBee_Transmitter (saved by Fritzing 0.9.3b)
breadboards: 1

parts:
  Raspberry_Pi_1 = Raspberry Pi 3 [part_number=RPI-3-V1.2]
  S1 = Momentary Switch [package=ksa_sealed_tac_switch]
  U1 = XBEE-1 [package=xbee-1]
  S2 = Momentary Switch [package=ksa_sealed_tac_switch]
  S3 = Momentary Switch [package=ksa_sealed_tac_switch]
  S4 = Momentary Switch [package=ksa_sealed_tac_switch]

nets:
  3V3: Raspberry_Pi_1.3v3, U1.VDD
  N1: Raspberry_Pi_1.GPIO5, S4.1
  N2: Raspberry_Pi_1.GPIO6, S1.3
  N3: Raspberry_Pi_1.GPIO13, S2.1, S2.2
  N4: Raspberry_Pi_1.GPIO19, S3.1, S3.2
  GND: Raspberry_Pi_1.GND, S1.1, U1.GND, S2.3, S2.4, S3.3, S3.4, S4.3
  N5: Raspberry_Pi_1.GPIO15, U1.DOUT
  N6: Raspberry_Pi_1.GPIO14, U1.DIN

notes:
  Model: S1
