# Fritzing sketch Arduino_Motor_Board_DC_Motor (saved by Fritzing 0.9.3b)
breadboards: 1

parts:
  Raspberry_Pi_1 = Raspberry Pi 3 [part_number=RPI-3-V1.2]
  Power_plug1 = Power plug
  Part1 = Adafruit Motor/Stepper/Servo Shield [part_number="Adafruit #1438"]
  M1 = DC Motor

nets:
  N1: Raspberry_Pi_1.GPIO2, Part1.AD4/SDA
  N2: Raspberry_Pi_1.GPIO3, Part1.AD5/SCL
  GND: Raspberry_Pi_1.GND, Power_plug1.GND, Part1.GND
  5V: Raspberry_Pi_1.5V, Part1.+5V
  N3: Power_plug1.VCC, Part1.VMOTOR
  N4: Part1.M1B, M1.pin_1
  N5: Part1.M1A, M1.pin_2

notes:
  +5V External Supply
  Common Ground
  I2C

custom parts:
  Adafruit Motor/Stepper/Servo Shield: The original Adafruit Motorshield kit is one of our most beloved kits, which is why we decided to make something even better. We have upgraded the shield kit to make the bestest, easiest way to drive DC and Stepper motors. This shield will make quick work of your next robotics project! We kept the ability to drive up to 4 DC motors or 2 stepper motors, but added many improvements: Instead of a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
