# Fritzing sketch Joystick_Controlled_XBee_Robot__Robot (saved by Fritzing 0.9.3b)
breadboards: 1

parts:
  Raspberry_Pi_1 = Raspberry Pi 3 [part_number=RPI-3-V1.2]
  Part1 = Adafruit Motor/Stepper/Servo Shield [part_number="Adafruit #1438"]
  M1 = DC Motor
  Raspberry_Pi_Zero1 = Raspberry Pi Zero  # not connected
  M2 = DC Motor
  Part2 = Breadboard Power Supply Board SMD
  VCC1 = 4 x AAA Battery Mount
  Power_plug1 = Power plug  # not connected
  U2 = XBEE-1 [package=xbee-1]
  LED1 = smd LED [color="Green (555nm)" package="0603 [SMD]"]
  R1 = Resistor [tolerance=±5% resistance=220 package="0603 [SMD]"]
  J2 = Piezo Speaker

nets:
  3V3: Raspberry_Pi_1.3v3, U2.VDD
  N1: Raspberry_Pi_1.GPIO2, Part1.AD4/SDA
  N2: Raspberry_Pi_1.GPIO3, Part1.AD5/SCL
  N3: Raspberry_Pi_1.GPIO19, J2.pin2
  N4: Raspberry_Pi_1.GPIO21, LED1.anode
  N5: Raspberry_Pi_1.GPIO15, U2.DOUT
  N6: Raspberry_Pi_1.GPIO14, U2.DIN
  GND: Raspberry_Pi_1.GND, Part1.GND, Part2.GND, U2.GND, R1.Pin_0, J2.pin1
  5V: Raspberry_Pi_1.5V, Part1.+5V
  N7: Part1.M2A, M2.pin_1
  N8: Part1.M2B, M2.pin_2
  N9: Part1.M1B, M1.pin_1
  N10: Part1.M1A, M1.pin_2
  N11: Part1.VMOTOR, Part2.VCC
  N12: Part2.VIN, VCC1.+
  N13: LED1.cathode, R1.Pin_1

notes:
  +5V Regulated Supply
  I2C
  +5V >1000MA USB Supply
  Pi 3 Zero WH
  Model: S1
  Robot Motors

custom parts:
  Adafruit Motor/Stepper/Servo Shield: The original Adafruit Motorshield kit is one of our most beloved kits, which is why we decided to make something even better. We have upgraded the shield kit to make the bestest, easiest way to drive DC and Stepper motors. This shield will make quick work of your next robotics project! We kept the ability to drive up to 4 DC motors or 2 stepper motors, but added many improvements: Instead of a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
