# Fritzing sketch Dual_LCD_Displays (saved by Fritzing 0.8.7b)
breadboards: 1

parts:
  Raspberry_Pi_Zero1 = Raspberry Pi Zero
  LCD1 = 16x4 LCD display [part_number=1604A]
  LCD2 = 16x2 LCD display [part_number=1602A]
  R2 = Rotary Potentiometer (Small) [maximum_resistance=100kΩ package=THT]
  R3 = Rotary Potentiometer (Small) [maximum_resistance=100kΩ package=THT]
  R4 = Rotary Potentiometer (Small) [maximum_resistance=100kΩ package=THT]

nets:
  N1: Raspberry_Pi_Zero1.GPIO2, LCD2.RS
  N2: Raspberry_Pi_Zero1.GPIO3, LCD2.E
  N3: Raspberry_Pi_Zero1.GIPO27, LCD1.DB7
  N4: Raspberry_Pi_Zero1.GIPO22, LCD1.DB6
  N5: Raspberry_Pi_Zero1.GIPO11, LCD2.DB7
  N6: Raspberry_Pi_Zero1.GIPO5, LCD2.DB6
  N7: Raspberry_Pi_Zero1.GIPO6, LCD2.DB5
  N8: Raspberry_Pi_Zero1.GIPO13, LCD2.DB4
  N9: Raspberry_Pi_Zero1.GIPO19, LCD1.E
  N10: Raspberry_Pi_Zero1.GIPO26, LCD1.RS
  N11: Raspberry_Pi_Zero1.GIPO25, LCD1.DB4
  N12: Raspberry_Pi_Zero1.GIPO24, LCD1.DB5
  VSS: Raspberry_Pi_Zero1.GND, LCD1.Vss, LCD1.R/W, LCD2.Vss, LCD2.R/W, R2.leg2, R4.leg2
  N13: Raspberry_Pi_Zero1.GIPO14, LCD2.LED-
  VDD: Raspberry_Pi_Zero1.5V, LCD1.Vdd, LCD2.Vdd, R2.leg1, R3.wiper
  N14: LCD1.Vo, R2.wiper
  N15: LCD2.Vo, R4.wiper
  N16: LCD2.LED+, R3.leg2

notes:
  Contrast
  Brightness
  16x2 LCD
  With Backlight
  16x4 LCD
  No Backlight

custom parts:
  16x4 LCD display: 16x4 character display. CHECK LED POLARITY BEFORE CONNECTING POWER Some versions of the display have the polarity of the LED pins "A" and "K" reversed.
  16x2 LCD display: 16x2 character display. CHECK LED POLARITY BEFORE CONNECTING POWER Some versions of the display have the polarity of the LED pins "A" and "K" reversed.
