# Fritzing sketch Button (saved by Fritzing 0.9.3b)
breadboards: 1

parts:
  Raspberry_Pi_1 = Raspberry Pi 3 [part_number=RPI-3-V1.2]
  S1 = Momentary Switch [package=ksa_sealed_tac_switch]

nets:
  N1: Raspberry_Pi_1.GPIO24, S1.2
  N2: Raspberry_Pi_1.GPIO14, Raspberry_Pi_1.GND, S1.4
