# Fritzing sketch 7Segment_LED_Display (saved by Fritzing 0.9.3b)
breadboards: 1

parts:
  Raspberry_Pi_1 = Raspberry Pi 3 [part_number=RPI-3-V1.2]
  7_Segment1 = 7 Segment Display
  R13 = Resistor [tolerance=±5% resistance=220 package="2010 [SMD]"]
  R14 = Resistor [tolerance=±5% resistance=220 package="2010 [SMD]"]
  R15 = Resistor [tolerance=±5% resistance=220 package="2010 [SMD]"]
  R16 = Resistor [tolerance=±5% resistance=220 package="2010 [SMD]"]
  R17 = Resistor [tolerance=±5% resistance=220 package="2010 [SMD]"]
  R18 = Resistor [tolerance=±5% resistance=220 package="2010 [SMD]"]
  R19 = Resistor [tolerance=±5% resistance=220 package="2010 [SMD]"]

nets:
  N1: Raspberry_Pi_1.GPIO2, R16.Pin_0
  N2: Raspberry_Pi_1.GPIO3, R17.Pin_0
  N3: Raspberry_Pi_1.GPIO4, R18.Pin_1
  N4: Raspberry_Pi_1.GPIO17, R19.Pin_1
  N5: Raspberry_Pi_1.GPIO27, R13.Pin_0
  N6: Raspberry_Pi_1.GPIO22, R14.Pin_0
  N7: Raspberry_Pi_1.GPIO10, R15.Pin_1
  N8: Raspberry_Pi_1.GND, 7_Segment1.common_cathode
  N9: 7_Segment1.Segment_E, R13.Pin_1
  N10: 7_Segment1.Segment_D, R14.Pin_1
  N11: 7_Segment1.Segment_C, R15.Pin_0
  N12: 7_Segment1.Segment_B, R19.Pin_0
  N13: 7_Segment1.Segment_A, R18.Pin_0
  N14: 7_Segment1.Segment_F, R17.Pin_1
  N15: 7_Segment1.Segment_G, R16.Pin_1
