# Fritzing sketch Photocell (saved by Fritzing 0.9.3b)
breadboards: 1

parts:
  Raspberry_Pi_1 = Raspberry Pi 3 [part_number=RPI-3-V1.2]
  C1 = Electrolytic Capacitor [capacitance=1µF package="1010 [SMD, electrolytic]"]
  R1 = PHOTOCELL [package=photocell]

nets:
  N1: Raspberry_Pi_1.3v3, R1.P$2
  N2: Raspberry_Pi_1.GPIO2, C1.-, R1.P$1
  N3: Raspberry_Pi_1.GND, C1.+
