# Fritzing sketch line-follower-bot (saved by Fritzing 0.8.7b)
breadboards: 1

parts:
  Part1 = Adafruit Motor/Stepper/Servo Shield [part_number="Adafruit #1438"]
  Part2 = Arduino Uno (Rev3)
  M1 = DC Motor
  M2 = DC Motor
  VCC1 = Battery
  U1 = SWITCH-SPST-2 [package=r_sw_th]
  M3 = fc-51 [package=THT]
  M4 = fc-51 [package=THT]

nets:
  N1: Part1.M3A, M2.pin_2
  N2: Part1.M3B, M2.pin_1
  N3: Part1.M4B, M1.pin_2
  N4: Part1.M4A, M1.pin_1
  +5V: Part1.+5V, Part2.5V
  N5: Part1.AD4/SDA, Part2.A4/SDA
  N6: Part1.AD5/SCL, Part2.A5/SCL
  N7: Part2.D8, M3.pin1
  N8: Part2.GND, M3.pin2, M4.pin2
  N9: Part2.D7, M4.pin1
  N10: Part2.3V3, M3.pin3, M4.pin3
  N11: VCC1.-, U1.P

notes:
  Power Unit
  I2C
  Sensor Unit
  +3.3V
  IR Sensors
  Wheel Motors
  Arduino Duemilanove
  Adafruit Motor Shield

custom parts:
  Adafruit Motor/Stepper/Servo Shield: The original Adafruit Motorshield kit is one of our most beloved kits, which is why we decided to make something even better. We have upgraded the shield kit to make the bestest, easiest way to drive DC and Stepper motors. This shield will make quick work of your next robotics project! We kept the ability to drive up to 4 DC motors or 2 stepper motors, but added many improvements: Instead of a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
