# Fritzing sketch sensor-bot (saved by Fritzing 0.8.7b)
breadboards: 2

parts:
  Part1 = Adafruit Motor/Stepper/Servo Shield [part_number="Adafruit #1438"]
  Part2 = Arduino Uno (Rev3)
  M1 = DC Motor
  M2 = DC Motor
  VCC1 = Battery
  U1 = SWITCH-SPST-2 [package=r_sw_th]
  Part3 = HC-SR04 Ultrasonic Rangemeter

nets:
  N1: Part1.M3A, M2.pin_2
  N2: Part1.M3B, M2.pin_1
  N3: Part1.M4B, M1.pin_2
  N4: Part1.M4A, M1.pin_1
  +5V: Part1.+5V, Part2.5V, Part3.VCC
  N5: Part1.AD4/SDA, Part2.A4/SDA
  N6: Part1.AD5/SCL, Part2.A5/SCL
  GND: Part1.GND, Part2.GND, VCC1.+, Part3.GND
  VIN: Part1.VIN, Part2.VIN, U1.O
  N7: Part2.D12/MISO, Part3.Echo
  N8: Part2.D13/SCK, Part3.Trig
  N9: VCC1.-, U1.P

notes:
  Power Unit
  I2C
  Sensor Unit

custom parts:
  Adafruit Motor/Stepper/Servo Shield: The original Adafruit Motorshield kit is one of our most beloved kits, which is why we decided to make something even better. We have upgraded the shield kit to make the bestest, easiest way to drive DC and Stepper motors. This shield will make quick work of your next robotics project! We kept the ability to drive up to 4 DC motors or 2 stepper motors, but added many improvements: Instead of a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
