# Fritzing sketch 16x2_LCD (saved by Fritzing 0.9.3b)
breadboards: 1

parts:
  LCD1 = LCD screen
  Raspberry_Pi_1 = Raspberry Pi 3 [part_number=RPI-3-V1.2]
  R1 = Rotary Potentiometer (Small) [maximum_resistance=100kΩ package=THT]
  R2 = Rotary Potentiometer (Small) [maximum_resistance=100kΩ package=THT]

nets:
  VSS: LCD1.VSS, LCD1.R/W, LCD1.LED-, Raspberry_Pi_1.GND, R2.leg2
  VDD: LCD1.VDD, Raspberry_Pi_1.5V, R1.wiper
  N1: LCD1.V0, R2.wiper
  N2: LCD1.RS, Raspberry_Pi_1.GPIO26
  N3: LCD1.E, Raspberry_Pi_1.GPIO19
  N4: LCD1.DB4, Raspberry_Pi_1.GPIO13
  N5: LCD1.DB5, Raspberry_Pi_1.GPIO6
  N6: LCD1.DB6, Raspberry_Pi_1.GPIO5
  N7: LCD1.DB7, Raspberry_Pi_1.GPIO11
  N8: LCD1.LED+, R1.leg2

notes:
  Contrast
  Brightness
