# Fritzing sketch Servo (saved by Fritzing 0.9.3b)
breadboards: 1

parts:
  Raspberry_Pi_1 = Raspberry Pi 3 [part_number=RPI-3-V1.2]
  J1 = Basic Servo
  VCC1 = 4 x AAA Battery Mount
  R1 = Resistor [tolerance=±5% resistance=1k package="0603 [SMD]"]

nets:
  N1: Raspberry_Pi_1.GPIO27, R1.Pin_0
  GND: Raspberry_Pi_1.GND, J1.gnd, VCC1.-
  N2: J1.vcc, VCC1.+
  N3: J1.pulse, R1.Pin_1
