# Fritzing sketch XBee_Receiver (saved by Fritzing 0.9.3b)
breadboards: 1

parts:
  Raspberry_Pi_1 = Raspberry Pi 3 [part_number=RPI-3-V1.2]
  U1 = XBEE-1 [package=xbee-1]
  LED1 = LED - 5mm [color="Red (633nm)" package="5 mm [THT]"]  # not connected
  LED2 = LED - 5mm [color="Red (633nm)" package="5 mm [THT]"]
  LED3 = LED - 5mm [color="Red (633nm)" package="5 mm [THT]"]
  LED4 = LED - 5mm [color="Red (633nm)" package="5 mm [THT]"]
  R1 = Resistor [tolerance=±5% resistance=270 package=THT]
  R2 = Resistor [tolerance=±5% resistance=270 package=THT]
  R4 = Resistor [tolerance=±5% resistance=270 package=THT]
  R5 = Resistor [tolerance=±5% resistance=270 package=THT]

nets:
  3V3: Raspberry_Pi_1.3v3, U1.VDD
  N1: Raspberry_Pi_1.GPIO20, LED4.anode
  N2: Raspberry_Pi_1.GPIO16, LED3.anode
  N3: Raspberry_Pi_1.GPIO12, LED2.anode
  GND: Raspberry_Pi_1.GND, U1.GND, R1.Pin_1, R2.Pin_0, R4.Pin_0, R5.Pin_0
  N4: Raspberry_Pi_1.GPIO15, U1.DOUT
  N5: Raspberry_Pi_1.GPIO14, U1.DIN
  N6: LED2.cathode, R1.Pin_0
  N7: LED3.cathode, R4.Pin_1
  N8: LED4.cathode, R2.Pin_1

notes:
  Model: S1
