# Fritzing sketch Analog_Joystick_No_ADC (saved by Fritzing 0.9.3b)
breadboards: 1

parts:
  Raspberry_Pi_1 = Raspberry Pi 3 [part_number=RPI-3-V1.2]
  C2 = Ceramic Capacitor [capacitance="100 nF" package="1206 [SMD, multilayer]"]
  Part1 = Thumb Joystick
  R1 = Resistor [tolerance=±5% resistance=1k package=THT]
  R2 = Resistor [tolerance=±5% resistance=1k package=THT]

nets:
  3V3: Raspberry_Pi_1.3v3, Part1.VCC
  N1: Raspberry_Pi_1.GPIO19, R1.Pin_1
  N2: Raspberry_Pi_1.GPIO26, R2.Pin_0
  N3: Raspberry_Pi_1.GND, C2.0
  N4: C2.1, Part1.GND, R1.Pin_0
  N5: Part1.HORZ, R2.Pin_1

notes:
  100nF
  Ceramic Cap
