# Fritzing sketch Joystick_Controlled_XBee_Robot__Controller (saved by Fritzing 0.9.3b)
breadboards: 1

parts:
  Raspberry_Pi_1 = Raspberry Pi 3 [part_number=RPI-3-V1.2]
  Part1 = Thumb Joystick
  IC1 = MCP3008 8-channel 10-bit ADC [part_number=MCP3008]
  U3 = XBEE-1 [package=xbee-1]
  S1 = Momentary Switch [package=ksa_sealed_tac_switch]

nets:
  3V3: Raspberry_Pi_1.3v3, Part1.VCC, IC1.no_name_yet#15, IC1.no_name_yet#16, U3.VDD
  N1: Raspberry_Pi_1.GPIO10, IC1.no_name_yet#11
  N2: Raspberry_Pi_1.GPIO9, IC1.no_name_yet#12
  N3: Raspberry_Pi_1.GPIO11, IC1.no_name_yet#13
  N4: Raspberry_Pi_1.GPIO5, IC1.no_name_yet#10
  N5: Raspberry_Pi_1.GPIO12, S1.2
  GND: Raspberry_Pi_1.GND, Part1.GND, U3.GND, S1.4
  N6: Raspberry_Pi_1.GPIO15, U3.DOUT
  N7: Raspberry_Pi_1.GPIO14, U3.DIN
  N8: Part1.HORZ, IC1.no_name_yet#1
  N9: Part1.VERT, IC1.no_name_yet#2
  N10: IC1.no_name_yet#9, IC1.no_name_yet#14

notes:
  Model: S1
  Light Control
