# Fritzing sketch OLED_Display (saved by Fritzing 0.8.7b)

parts:
  Raspberry_Pi_Zero1 = Raspberry Pi Zero
  OLED1 = OLED 128x64 I2C Monochrome Display

nets:
  3V3: Raspberry_Pi_Zero1.3v3, OLED1.VDD
  N1: Raspberry_Pi_Zero1.GPIO2, OLED1.SDA
  N2: Raspberry_Pi_Zero1.GPIO3, OLED1.SCK
  GND: Raspberry_Pi_Zero1.GND, OLED1.GND

notes:
  I2C
  SD 1306
  128x64
  OLED
