# Fritzing sketch RF_433MHz_RX_TX (saved by Fritzing 0.8.7b)

parts:
  Raspberry_Pi_Zero1 = Raspberry Pi Zero
  U6 = RF-LINK_TX [package=rf-link_tx]
  U7 = RF-LINK_RX [package=rf-link_rx]

nets:
  N1: Raspberry_Pi_Zero1.GIPO17, U6.DATA
  N2: Raspberry_Pi_Zero1.GIPO27, U7.Data
  GND: Raspberry_Pi_Zero1.GND, U6.GND, U7.GND
  5V: Raspberry_Pi_Zero1.5V, U6.+5V, U7.VCC

notes:
  433MHz
  Transmitter
  433MHz
  Receiver

custom parts:
  RF-LINK_TX: Common RF transmitter of the 315.00Mhz varity
  RF-LINK_RX: RF Link receivers- WRL-8947, 8948, 8949, 8950
